# Fritzing sketch shemas (saved by Fritzing 0.9.3b)
breadboards: 1

parts:
  Composant1 = Arduino Uno (Rev3)
  Composant2 = Bluetooth HC-05 Macho
  S1 = SWITCH-MOMENTARY-2 [package=tactile-pth]  # not connected
  R1 = Resistor [tolerance=±5% resistance=330 package=THT]
  LED1 = LED - 5mm [color="Red (633nm)" package="5 mm [THT]"]
  R2 = Resistor [tolerance=±5% resistance=330 package=THT]

nets:
  N1: Composant1.D10_PWM/SS, R1.Pin_0
  N2: Composant1.D13/SCK, R2.Pin_1
  N3: Composant1.D0/RX, Composant2.TXD
  N4: Composant1.D1/TX, Composant2.RXD
  5V: Composant1.5V, Composant2.VCC
  GND: Composant1.GND, Composant2.GND, R1.Pin_1, LED1.cathode
  N5: LED1.anode, R2.Pin_0
